# Fritzing sketch 13 (saved by Fritzing 0.9.3b)
breadboards: 1

parts:
  LED2 = LED - 5mm [color="Yellow (595nm)" package="5 mm [THT]"]
  LED3 = LED - 5mm [color="Green (570nm)" package="5 mm [THT]"]
  R2 = Resistor [tolerance=±5% resistance=220 package="0603 [SMD]"]
  LED4 = LED - 5mm [color="Green (570nm)" package="5 mm [THT]"]
  R3 = Resistor [tolerance=±5% resistance=220 package="0603 [SMD]"]
  R4 = Resistor [tolerance=±5% resistance=220 package="0603 [SMD]"]
  U1 = LuaNode32 / ESP32 [part_number=ESP32S-PIN30]
  R5 = Resistor [tolerance=±5% resistance=220 package="0603 [SMD]"]
  LED5 = LED - 5mm [color="Red (635nm)" package="5 mm [THT]"]

nets:
  N1: LED2.cathode, LED3.cathode, LED4.cathode, U1.GND, LED5.cathode
  N2: LED2.anode, R2.Pin_0
  N3: LED3.anode, R3.Pin_0
  N4: R2.Pin_1, U1.TX2
  N5: LED4.anode, R4.Pin_0
  N6: R3.Pin_1, U1.RX2
  N7: R4.Pin_1, U1.D4
  N8: U1.D5, R5.Pin_1
  N9: R5.Pin_0, LED5.anode

custom parts:
  LuaNode32 / ESP32: New Image for LuaNode32 DOIT ESP32 DEVKIT V1. Base parts from LuaNode32 / ESP32 ESP32 based LuaNode32 by G.Noorlander DOIT Esp32 DevKit v1 (30 pins long, 11 pins width) by Werner Rothschopf (modified by vanepp Dec 2018)
