# Fritzing sketch proyectofinal - copia (saved by Fritzing 0.9.3b)
breadboards: 1

parts:
  U2 = LuaNode32 / ESP32 [part_number=ESP32S-PIN30]
  LED1 = RGB LED (com. cathode, rgb) [package="5 mm [THT]"]
  R1 = Resistor [tolerance=±5% resistance=220 package="1206 [SMD]"]
  R2 = Resistor [tolerance=±20% resistance=220 package="1206 [SMD]"]
  R3 = Resistor [tolerance=±5% resistance=220 package="1206 [SMD]"]
  R4 = Resistor [tolerance=±5% resistance=100 package=THT]
  SG1 = Buzzer 12mm [package=buzzer-12mm-ns]
  S1 = Pushbutton [package="[THT]"]
  S2 = Pushbutton [package="[THT]"]
  S3 = Pushbutton [package="[THT]"]
  R5 = Resistor [tolerance=±5% resistance=100 package=THT]
  R6 = Resistor [tolerance=±5% resistance=100 package=THT]
  R7 = Resistor [tolerance=±5% resistance=100 package=THT]
  R8 = Resistor [tolerance=±5% resistance=220 package=THT]
  LED2 = LED - 5mm [color="Red (633nm)" package="5 mm [THT]"]
  Componente1 = MQ-4
  J1 = Basic Servo
  R10 = Resistor [tolerance=±5% resistance=100 package=THT]
  S4 = Pushbutton [package="[THT]"]
  R11 = Resistor [tolerance=±5% resistance=100 package=THT]
  PIR1 = PIR sensor

nets (from the breadboard view):
  N1: U2.D34, S3.Pin_3, S3.Pin_4, R7.Pin_0
  N2: U2.D35, S2.Pin_3, S2.Pin_4, R6.Pin_0
  N3: U2.D32, S1.Pin_3, S1.Pin_4, R5.Pin_0
  N4: U2.D27, PIR1.SIG
  N5: U2.D14, S4.Pin_3, S4.Pin_4, R11.Pin_0
  N6: U2.D12, J1.pulse
  N7: U2.D13, R10.Pin_0
  GND: U2.GND, LED1.common_cathode, SG1.2, R5.Pin_1, R6.Pin_1, R7.Pin_1, LED2.cathode, Componente1.GND, J1.gnd, R11.Pin_1, PIR1.GND
  VCC: U2.3V3, S1.Pin_1, S1.Pin_2, S2.Pin_1, S2.Pin_2, S3.Pin_1, S3.Pin_2, Componente1.VCC, J1.vcc, S4.Pin_1, S4.Pin_2, PIR1.VDD
  N8: U2.D15, R3.Pin_0
  N9: U2.D2, R2.Pin_0
  N10: U2.D4, R8.Pin_1
  N11: U2.RX2, R1.Pin_0
  N12: U2.TX2, R4.Pin_0
  N13: LED1.red_anode, R1.Pin_1
  N14: LED1.green_anode, R2.Pin_1
  N15: LED1.blue_anode, R3.Pin_1
  N16: R4.Pin_1, SG1.1
  N17: R8.Pin_0, LED2.anode
  N18: Componente1.DO, R10.Pin_1

custom parts:
  LuaNode32 / ESP32: New Image for LuaNode32 DOIT ESP32 DEVKIT V1. Base parts from LuaNode32 / ESP32 ESP32 based LuaNode32 by G.Noorlander DOIT Esp32 DevKit v1 (30 pins long, 11 pins width) by Werner Rothschopf (modified by vanepp Dec 2018)
