# Fritzing sketch proyectofinal (saved by Fritzing 0.9.3b)
breadboards: 1

parts:
  U2 = LuaNode32 / ESP32 [part_number=ESP32S-PIN30]
  LED1 = RGB LED (com. cathode, rgb) [package="5 mm [THT]"]
  R1 = Resistor [tolerance=±5% resistance=220 package="1206 [SMD]"]
  R2 = Resistor [tolerance=±20% resistance=220 package="1206 [SMD]"]
  R3 = Resistor [tolerance=±5% resistance=220 package="1206 [SMD]"]
  R4 = Resistor [tolerance=±5% resistance=100 package=THT]
  SG1 = Buzzer 12mm [package=buzzer-12mm-ns]
  Componente1 = MQ-4
  J1 = Basic Servo
  R10 = Resistor [tolerance=±5% resistance=100 package=THT]
  S4 = Pushbutton [package="[THT]"]
  R11 = Resistor [tolerance=±5% resistance=100 package=THT]
  PIR1 = PIR sensor
  RHT1 = Humidity and Temperature Sensor RHT03

nets:
  N1: U2.D14, S4.Pin_3, S4.Pin_4, R11.Pin_0
  N2: U2.D12, J1.pulse
  N3: U2.D13, R10.Pin_0
  VCC: U2.3V3, Componente1.VCC, J1.vcc, S4.Pin_1, S4.Pin_2, PIR1.VDD, RHT1.Vcc
  GND: U2.GND, LED1.common_cathode, SG1.2, Componente1.GND, J1.gnd, R11.Pin_1, PIR1.GND, RHT1.GND_2
  N4: U2.D15, U2.RX2, R1.Pin_0, R3.Pin_0
  N5: U2.D2, R2.Pin_0
  N6: U2.TX2, R4.Pin_0
  N7: U2.D5, PIR1.SIG
  N8: U2.D21, RHT1.Data-signal
  N9: LED1.red_anode, R1.Pin_1
  N10: LED1.green_anode, R2.Pin_1
  N11: LED1.blue_anode, R3.Pin_1
  N12: R4.Pin_1, SG1.1
  N13: Componente1.DO, R10.Pin_1

custom parts:
  LuaNode32 / ESP32: New Image for LuaNode32 DOIT ESP32 DEVKIT V1. Base parts from LuaNode32 / ESP32 ESP32 based LuaNode32 by G.Noorlander DOIT Esp32 DevKit v1 (30 pins long, 11 pins width) by Werner Rothschopf (modified by vanepp Dec 2018)
