# Fritzing sketch 17 (saved by Fritzing 0.9.3b)
breadboards: 1

parts:
  U2 = LuaNode32 / ESP32 [part_number=ESP32S-PIN30]
  LED1 = RGB LED (com. cathode, rgb) [package="5 mm [THT]"]
  R1 = Resistor [tolerance=±5% resistance=220 package="1206 [SMD]"]
  R2 = Resistor [tolerance=±5% resistance=220 package="1206 [SMD]"]
  R3 = Resistor [tolerance=±5% resistance=220 package="1206 [SMD]"]
  SG1 = Buzzer 12mm [package=buzzer-12mm-ns]
  R4 = Resistor [tolerance=±5% resistance=100 package=THT]

nets:
  N1: U2.GND, LED1.common_cathode, SG1.2
  N2: U2.D15, R1.Pin_0
  N3: U2.D2, R2.Pin_0
  N4: U2.D4, R3.Pin_0
  N5: U2.RX2, R4.Pin_0
  N6: LED1.red_anode, R1.Pin_1
  N7: LED1.green_anode, R2.Pin_1
  N8: LED1.blue_anode, R3.Pin_1
  N9: SG1.1, R4.Pin_1

custom parts:
  LuaNode32 / ESP32: New Image for LuaNode32 DOIT ESP32 DEVKIT V1. Base parts from LuaNode32 / ESP32 ESP32 based LuaNode32 by G.Noorlander DOIT Esp32 DevKit v1 (30 pins long, 11 pins width) by Werner Rothschopf (modified by vanepp Dec 2018)
