# Fritzing sketch Esquema (saved by Fritzing 0.9.3b)
breadboards: 2

parts:
  U1 = LuaNode32 / ESP32 [part_number=ESP32S-PIN30]
  LED1 = LED - 5mm [color="Red (633nm)" package="5 mm [THT]"]
  R1 = Resistor [tolerance=±5% resistance=220 package=THT]
  R2 = Resistor [tolerance=±5% resistance=220 package=THT]
  S1 = Pushbutton [package="[THT]"]
  LED2 = LED - 5mm [color="Red (633nm)" package="5 mm [THT]"]
  R3 = Resistor [tolerance=±5% resistance=220 package=THT]
  R4 = Resistor [tolerance=±5% resistance=220 package=THT]
  S2 = Pushbutton [package="[THT]"]

nets:
  N1: U1.D14, R4.Pin_1, S2.Pin_3, S2.Pin_4
  N2: U1.D13, R3.Pin_1
  N3: U1.GND, LED1.cathode, R2.Pin_0
  N4: U1.3V3, S1.Pin_1, S1.Pin_2, LED2.cathode, R4.Pin_0, S2.Pin_1, S2.Pin_2
  N5: U1.D2, R1.Pin_1
  N6: U1.D4, R2.Pin_1, S1.Pin_3, S1.Pin_4
  N7: LED1.anode, R1.Pin_0
  N8: LED2.anode, R3.Pin_0

custom parts:
  LuaNode32 / ESP32: New Image for LuaNode32 DOIT ESP32 DEVKIT V1. Base parts from LuaNode32 / ESP32 ESP32 based LuaNode32 by G.Noorlander DOIT Esp32 DevKit v1 (30 pins long, 11 pins width) by Werner Rothschopf (modified by vanepp Dec 2018)
