# Fritzing sketch asignacion13 (saved by Fritzing 0.9.4)
breadboards: 1

parts:
  M1 = DOIT Esp32 DevKit v1 (30 pins long, 11 pins width) [part_number=ESP32S-PIN30]
  R1 = Resistor [tolerance=±5% resistance=220 package=THT]
  R2 = Resistor [tolerance=±5% resistance=220 package=THT]
  R3 = Resistor [tolerance=±5% resistance=220 package=THT]
  R4 = Resistor [tolerance=±5% resistance=220 package=THT]
  LED2 = LED - 5mm [color="Red (635nm)" package="5 mm [THT]"]
  LED3 = LED - 5mm [color="Blue (525nm)" package="5 mm [THT]"]
  LED4 = LED - 5mm [color="Orange (620nm)" package="5 mm [THT]"]
  LED5 = LED - 5mm [color="Yellow (574nm)" package="5 mm [THT]"]

nets:
  N1: M1.GND, LED2.cathode, LED3.cathode, LED4.cathode, LED5.cathode
  N2: M1.D4, R4.Pin_0
  N3: M1.RX2, R3.Pin_0
  N4: M1.TX2, R2.Pin_0
  N5: M1.D5, R1.Pin_0
  N6: R1.Pin_1, LED2.anode
  N7: R2.Pin_1, LED3.anode
  N8: R3.Pin_1, LED4.anode
  N9: R4.Pin_1, LED5.anode

custom parts:
  DOIT Esp32 DevKit v1 (30 pins long, 11 pins width): The DOIT Esp32 DevKit v1 is one of the development board created by DOIT to evaluate the ESP-WROOM-32 module. It is based on the ESP32 microcontroller that boasts Wifi, Bluetooth, Ethernet and Low Power support all in a single chip. (vanepp) made breadboard work, adjusted pin numbering and labels and reduced size of schematic and cleaned up pcb. This chip is 30pins long (2 x15) and 11 pins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

// code stored in the sketch: leerSerie.ino


/*
* blinkSerial.ino
*
* Este programa hace que el LED de status del microcontrolador
* ESP32 DEVKIT DOIT de 30 pines o un LED conectado al pin 2,
* parpadee. Los periodos de estar encendido y apagado del led
* son iguales.
*
* Ademas en el monitor serial del IDE 2.0 de Arduino se despliega
* si el led esta prendido o apagado.
*
* No usa la funcion delay(). En lugar de ello utiliza la
* biblioteca NoDelay. Esto permite que otro codigo ejecute al
* mismo tiempo que se encuentra en el periodo de espera.
*/
#include <NoDelay.h>
// Pin a la que esta conectado el LED, GPIO2
const unsigned int PIN_LED = 2;
// Periodo en ms que dura encendido o apagado el LED
const long PERIODO = 500;
// Inicialmente el LED está apagado
int estadoLed = LOW;
// Velocidad de transmisión del puerto serie
const unsigned int BAUD_RATE = 115200;
// Crea una instancia de la clase noDelay
// que determina si han transcurrido PERIODO ms
noDelay pausa(PERIODO);
void setup() {
// Establece el pin PIN_LED (GPIO2) como de salida.
pinMode(PIN_LED, OUTPUT);
// Establece la velocidad de transmisión del puerto
// serie al valor BAUD_RATE
Serial.begin(BAUD_RATE);
}
void loop() {
// Verifica si es tiempo de prender/apagar el LED
if (pausa.update()) {
// Prender/apagar el LED
if (estadoLed == LOW) {
estadoLed = HIGH;
// Escribe mensaje al puerto serie
Serial.println("LED encendido");
} else {
estadoLed = LOW;
// Escribe mensaje al puerto serie
Serial.println("LED apagado");
}
digitalWrite(PIN_LED, estadoLed);
}
}
